// Logisim project custom.circ as structural Verilog: 13 circuits, main circuit main
module main (
  output [7:0] out_1
);

  AddMachine addmachine_1 (.out_2(out_1));  // open: out_1
endmodule

module \nand  (
  input  in_1,
  input  in_2,
  output out_3
);

  wire and_1_out;

  and and_1 (and_1_out, in_1, in_2);
  not not_1 (out_3, and_1_out);
endmodule

module \nor  (
  input  in_1,
  input  in_2,
  output out_3
);

  wire or_1_out;

  or or_1 (or_1_out, in_1, in_2);
  not not_1 (out_3, or_1_out);
endmodule

module \xor  (
  input  in_1,
  input  in_2,
  output out_3
);

  wire and_1_out, and_2_out, not_1_out, not_2_out;

  not not_1 (not_1_out, in_1);
  not not_2 (not_2_out, in_2);
  and and_1 (and_1_out, not_1_out, in_2);
  and and_2 (and_2_out, in_1, not_2_out);
  or or_1 (out_3, and_1_out, and_2_out);

  // Notes on the sheet:
  //   (not A * B) + (A * not B)
endmodule

module _2_to_1_mux (
  input  in_1,
  input  in_2,
  input  Selector,
  output out_4
);

  wire and_1_out, and_2_out, not_1_out;

  not not_1 (not_1_out, Selector);
  and and_1 (and_1_out, in_1, not_1_out);
  and and_2 (and_2_out, Selector, in_2);
  or or_1 (out_4, and_1_out, and_2_out);
endmodule

module _4_to_1_mux (
  input  in_1,
  input  in_2,
  input  in_3,
  input  in_4,
  input  in_5,
  input  in_6,
  input  in_7,
  input  in_8,
  input  in_9,
  input  in_10,
  input  in_11,
  input  in_12,
  output out_13,
  output out_14,
  output out_15,
  output out_16
);

  wire and_1_out, and_2_out, and_3_out, and_4_out, and_5_out, and_6_out, not_1_out, not_2_out, not_3_out,
       or_1_out, or_2_out;

  and and_1 (and_1_out, in_1, not_1_out);
  not not_1 (not_1_out, in_7);
  and and_2 (and_2_out, in_7, in_2);
  and and_3 (and_3_out, in_3, not_2_out);
  not not_2 (not_2_out, in_7);
  and and_4 (and_4_out, in_7, in_4);
  or or_1 (or_1_out, and_1_out, and_2_out);
  or or_2 (or_2_out, and_3_out, and_4_out);
  and and_5 (and_5_out, or_1_out, not_3_out);
  not not_3 (not_3_out, in_8);
  and and_6 (and_6_out, in_8, or_2_out);
  or or_3 (out_13, and_5_out, and_6_out);
  _2_to_1_mux u_2_to_1_mux_1 (.in_1(in_5), .in_2(in_6), .Selector(in_11), .out_4(out_14));
  _2_to_1_mux u_2_to_1_mux_2 (.in_1(in_9), .in_2(in_10), .Selector(in_11), .out_4(out_16));
  _2_to_1_mux u_2_to_1_mux_3 (.in_1(out_14), .in_2(out_16), .Selector(in_12), .out_4(out_15));

  // Notes on the sheet:
  //   Selector
endmodule

module AddMachine (
  output [7:0] out_1,
  output [7:0] out_2
);

  wire clock_1_out;

  Adder adder_1 (.a(8'h1), .b(out_2), .out(out_1));  // open: cin, cout
  Clock clock_1 (.out(clock_1_out));
  Register register_1 (.D(out_1), .Q(out_2), .clk(clock_1_out));  // open: en, clr
endmodule

module Ex4 (
  input  [7:0] in_1,
  output Out1,
  output [7:0] out_3
);

  wire [7:0] bit_extender_1_out, negator_1_out;

  assign bit_extender_1_out = {{1{1'b0}}, in_1[6:0]};  // Bit_Extender bit_extender_1
  and and_1 (Out1, in_1[0], in_1[7]);
  Negator negator_1 (.in(bit_extender_1_out), .out(negator_1_out));
  Multiplexer #(.width(8), .enable("false")) multiplexer_1 (
    .in0(bit_extender_1_out), .in1(negator_1_out), .out(out_3), .sel(in_1[7]));

  // Other names for the same wires on the sheet: bit0 = in_1[0]; bit7 = in_1[7]

  // Notes on the sheet:
  //   In
  //   2-to-1 mux
endmodule

module rotr (
  input  [15:0] in_1,
  input  [3:0] B,
  output [15:0] out_3
);

  wire bitselector_1_out, bitselector_2_out, bitselector_3_out, bitselector_4_out;
  wire [15:0] rotr8_1_out_3, rotr8_2_out_3, rotr8_3_out_3;

  rotr8 rotr8_1 (.in_1(in_1), .in_2(bitselector_1_out), .out_3(rotr8_1_out_3));
  BitSelector #(.width(4)) bitselector_1 (.in(B), .out(bitselector_1_out), .sel(2'b11));
  rotr8 rotr8_2 (.in_1(rotr8_1_out_3), .in_2(bitselector_2_out), .out_3(rotr8_2_out_3));
  BitSelector #(.width(4)) bitselector_2 (.in(B), .out(bitselector_2_out), .sel(2'b10));
  rotr8 rotr8_3 (.in_1(rotr8_2_out_3), .in_2(bitselector_4_out), .out_3(rotr8_3_out_3));
  BitSelector #(.width(4)) bitselector_3 (.in(B), .out(bitselector_3_out), .sel(2'b00));
  BitSelector #(.width(4)) bitselector_4 (.in(B), .out(bitselector_4_out), .sel(2'b01));
  rotr8 rotr8_4 (.in_1(rotr8_3_out_3), .in_2(bitselector_3_out), .out_3(out_3));

  // Notes on the sheet:
  //   A
endmodule

module rotr1 (
  input  [15:0] in_1,
  input  in_2,
  output [15:0] out_3
);

  Multiplexer #(.width(16), .enable("false")) multiplexer_1 (
    .in0(in_1), .in1({in_1[0], in_1[15:1]}), .out(out_3), .sel(in_2));
endmodule

module rotr2 (
  input  [15:0] in_1,
  input  in_2,
  output [15:0] out_3
);

  wire [15:0] rotr1_1_out_3, rotr1_2_out_3;

  rotr1 rotr1_1 (.in_1(in_1), .in_2(in_2), .out_3(rotr1_1_out_3));
  Multiplexer #(.width(16), .enable("false")) multiplexer_1 (.in0(in_1), .in1(rotr1_2_out_3), .out(out_3), .sel(in_2));
  rotr1 rotr1_2 (.in_1(rotr1_1_out_3), .in_2(in_2), .out_3(rotr1_2_out_3));
endmodule

module rotr4 (
  input  [15:0] in_1,
  input  in_2,
  output [15:0] out_3
);

  wire [15:0] rotr2_1_out_3, rotr2_2_out_3;

  rotr2 rotr2_1 (.in_1(in_1), .in_2(in_2), .out_3(rotr2_1_out_3));
  Multiplexer #(.width(16), .enable("false")) multiplexer_1 (.in0(in_1), .in1(rotr2_2_out_3), .out(out_3), .sel(in_2));
  rotr2 rotr2_2 (.in_1(rotr2_1_out_3), .in_2(in_2), .out_3(rotr2_2_out_3));
endmodule

module rotr8 (
  input  [15:0] in_1,
  input  in_2,
  output [15:0] out_3
);

  wire [15:0] rotr4_1_out_3, rotr4_2_out_3;

  rotr4 rotr4_1 (.in_1(in_1), .in_2(in_2), .out_3(rotr4_1_out_3));
  rotr4 rotr4_2 (.in_1(rotr4_1_out_3), .in_2(in_2), .out_3(rotr4_2_out_3));
  Multiplexer #(.width(16), .enable("false")) multiplexer_1 (.in0(in_1), .in1(rotr4_2_out_3), .out(out_3), .sel(in_2));
endmodule
