// Logisim project alu.circ as structural Verilog: 1 circuit, main circuit main
module main (
  input  [31:0] X,
  input  [31:0] Y,
  input  [3:0] Switch,
  output Equal,
  output [31:0] Result
);

  wire comparator_1_lt;
  wire [4:0] bit_extender_1_out;
  wire [31:0] op_add, op_and, op_div, op_mulh, op_mult, op_or, op_rem, op_sll, op_slt, op_sra, op_srl,
       op_xor, undriven;

  Adder #(.width(32)) adder_1 (.a(X), .b(Y), .out(op_add));  // open: cin, cout
  assign op_and = X & Y;  // AND_Gate and_1, 32 bits wide
  assign op_or = X | Y;  // OR_Gate or_1, 32 bits wide
  assign op_xor = X ^ Y;  // XOR_Gate xor_1, 32 bits wide
  Bit_Extender #(.in_width(32), .out_width(5)) bit_extender_1 (.in(Y), .out(bit_extender_1_out));
  Shifter #(.width(32), .shift("ar")) shifter_1 (.in(X), .\dist (bit_extender_1_out), .out(op_sra));
  Shifter #(.width(32), .shift("lr")) shifter_2 (.in(X), .\dist (bit_extender_1_out), .out(op_srl));
  Shifter #(.width(32)) shifter_3 (.in(X), .\dist (bit_extender_1_out), .out(op_sll));
  Multiplexer #(.select(4), .width(32), .enable("false")) multiplexer_1 (
    .in0(op_add), .in1(op_and), .in2(op_or), .in3(op_xor), .in4(op_srl), .in5(op_sra), .in6(op_sll),
    .in7(op_slt), .in8(op_div), .in9(op_rem), .in10(op_mult), .in11(op_mulh), .in12(undriven), .out(Result),
    .sel(Switch));  // open: in13, in14, in15
  Comparator #(.width(32)) comparator_1 (.a(X), .b(Y), .eq(Equal), .lt(comparator_1_lt));  // open: gt
  Divider #(.width(32)) divider_1 (.a(X), .b(Y), .out(op_div), .rem(op_rem));  // open: upper
  Multiplier #(.width(32)) multiplier_1 (.a(X), .b(Y), .out(op_mult), .cout(op_mulh));  // open: cin
  assign op_slt = {{31{1'b0}}, comparator_1_lt};  // Bit_Extender bit_extender_2

  // Other names for the same wires on the sheet: S[3:0] = Switch

  // Notes on the sheet:
  //   INPUTS to your circuit
  //   DON'T CHANGE THE LOCATIONS OF THE INPUTS AND OUTPUTS!
  //   OUTPUTS from your circuit
endmodule
