// Logisim project regfile.circ as structural Verilog: 1 circuit, main circuit main
module main (
  input  [4:0] Read_Register_1__rs1,
  input  [4:0] Read_Register_2__rs2,
  input  [4:0] Write_Register__rd,
  input  [31:0] Write_Data,
  input  Write_Enable,
  input  Clock,
  output [31:0] ra_Value,
  output [31:0] sp_Value,
  output [31:0] t0_Value,
  output [31:0] t1_Value,
  output [31:0] t2_Value,
  output [31:0] s0_Value,
  output [31:0] s1_Value,
  output [31:0] a0_Value,
  output [31:0] Read_Data_1,
  output [31:0] Read_Data_2
);

  wire _0, _1, _2, _5, _6, _7, _8, _9, _10, _11, and_6_out, and_7_out, and_8_out, and_9_out, and_10_out,
       and_11_out, and_12_out, and_13_out, and_14_out, demultiplexer_1_out0, demultiplexer_1_out1,
       demultiplexer_1_out2, demultiplexer_1_out5, demultiplexer_1_out6, demultiplexer_1_out7,
       demultiplexer_1_out8, demultiplexer_1_out9, demultiplexer_1_out10, demultiplexer_1_out11;
  wire [31:0] to1, to2, to5, to6, to7, to8, to9, to10, to11, x0, x11;

  and and_1 (_0, 1'b0, demultiplexer_1_out0);
  Multiplexer #(.select(5), .width(32), .enable("false")) multiplexer_1 (
    .in0(x0), .in1(ra_Value), .in2(sp_Value), .in3(x0), .in4(x0), .in5(t0_Value), .in6(t1_Value),
    .in7(t2_Value), .in8(s0_Value), .in9(s1_Value), .in10(a0_Value), .in11(x11), .in12(x0), .in13(x0),
    .in14(x0), .in15(x0), .in16(x0), .in17(x0), .in18(x0), .in19(x0), .in20(x0), .in21(x0), .in22(x0),
    .in23(x0), .in24(x0), .in25(x0), .in26(x0), .in27(x0), .in28(x0), .in29(x0), .in30(x0), .in31(x0),
    .out(Read_Data_1), .sel(Read_Register_1__rs1));
  and and_2 (_1, demultiplexer_1_out1, 1'b1);
  and and_3 (_2, demultiplexer_1_out2, 1'b1);
  Demultiplexer #(.select(5), .enable("false")) demultiplexer_1 (
    .out0(demultiplexer_1_out0), .out1(demultiplexer_1_out1), .out2(demultiplexer_1_out2),
    .out5(demultiplexer_1_out5), .out6(demultiplexer_1_out6), .out7(demultiplexer_1_out7),
    .out8(demultiplexer_1_out8), .out9(demultiplexer_1_out9), .out10(demultiplexer_1_out10),
    .out11(demultiplexer_1_out11), .in(1'b1), .sel(Write_Register__rd));  // open: out3, out4, out12, out13, out14, out15, out16, out17, out18, out19, out20, out21, out22, out23, out24, out25, out26, out27, out28, out29, out30, out31
  and and_4 (_6, demultiplexer_1_out6, 1'b1);
  and and_5 (_5, demultiplexer_1_out5, 1'b1);
  and and_6 (and_6_out, _1, Write_Enable);
  and and_7 (and_7_out, _2, Write_Enable);
  and and_8 (and_8_out, _5, Write_Enable);
  and and_9 (and_9_out, _6, Write_Enable);
  and and_10 (and_10_out, _8, Write_Enable);
  and and_11 (and_11_out, _8, Write_Enable);
  and and_12 (and_12_out, _9, Write_Enable);
  and and_13 (and_13_out, _10, Write_Enable);
  and and_14 (and_14_out, _11, Write_Enable);
  and and_15 (_8, demultiplexer_1_out8, 1'b1);
  and and_16 (_7, demultiplexer_1_out7, 1'b1);
  Multiplexer #(.select(5), .width(32), .enable("false")) multiplexer_2 (
    .in0(x0), .in1(ra_Value), .in2(sp_Value), .in3(x0), .in4(x0), .in5(t0_Value), .in6(t1_Value),
    .in7(t2_Value), .in8(s0_Value), .in9(s1_Value), .in10(a0_Value), .in11(x11), .in12(x0), .in13(x0),
    .in14(x0), .in15(x0), .in16(x0), .in17(x0), .in18(x0), .in19(x0), .in20(x0), .in21(x0), .in22(x0),
    .in23(x0), .in24(x0), .in25(x0), .in26(x0), .in27(x0), .in28(x0), .in29(x0), .in30(x0), .in31(x0),
    .out(Read_Data_2), .sel(Read_Register_2__rs2));
  and and_17 (_9, demultiplexer_1_out9, 1'b1);
  and and_18 (_10, demultiplexer_1_out10, 1'b1);
  and and_19 (_11, demultiplexer_1_out11, 1'b1);
  Register #(.width(32)) u_x0 (.en(_0), .Q(x0), .clk(Clock));  // open: D, clr
  Register #(.width(32)) x1 (.D(to1), .en(and_6_out), .Q(ra_Value), .clk(Clock));  // open: clr
  Register #(.width(32)) x2 (.D(to2), .en(and_7_out), .Q(sp_Value), .clk(Clock));  // open: clr
  Register #(.width(32)) x5 (.D(to5), .en(and_8_out), .Q(t0_Value), .clk(Clock));  // open: clr
  Register #(.width(32)) x6 (.D(to6), .en(and_9_out), .Q(t1_Value), .clk(Clock));  // open: clr
  Register #(.width(32)) x7 (.D(to7), .en(and_10_out), .Q(t2_Value), .clk(Clock));  // open: clr
  Register #(.width(32)) x8 (.D(to8), .en(and_11_out), .Q(s0_Value), .clk(Clock));  // open: clr
  Register #(.width(32)) x9 (.D(to9), .en(and_12_out), .Q(s1_Value), .clk(Clock));  // open: clr
  Register #(.width(32)) x10 (.D(to10), .en(and_13_out), .Q(a0_Value), .clk(Clock));  // open: clr
  Register #(.width(32)) u_x11 (.D(to11), .en(and_14_out), .Q(x11), .clk(Clock));  // open: clr
  Demultiplexer #(.select(5), .width(32), .enable("false")) demultiplexer_2 (
    .out1(to1), .out2(to2), .out5(to5), .out6(to6), .out7(to7), .out8(to8), .out9(to9), .out10(to10),
    .out11(to11), .in(Write_Data), .sel(Write_Register__rd));  // open: out0, out3, out4, out12, out13, out14, out15, out16, out17, out18, out19, out20, out21, out22, out23, out24, out25, out26, out27, out28, out29, out30, out31

  // Other names for the same wires on the sheet: clk = Clock; read_data1[31:0] = Read_Data_1;
  //   read_data2[31:0] = Read_Data_2; read_reg1[4:0] = Read_Register_1__rs1; read_reg2[4:0] = Read_Register_2__rs2;
  //   write_en = Write_Enable; write_reg[4:0] = Write_Register__rd; x1[31:0] = ra_Value; x2[31:0] = sp_Value;
  //   x5[31:0] = t0_Value; x6[31:0] = t1_Value; x7[31:0] = t2_Value; x8[31:0] = s0_Value; x9[31:0] = s1_Value;
  //   x10[31:0] = a0_Value

  // Notes on the sheet:
  //   INPUTS to your circuit
  //   These are DEBUG/TEST outputs from your circuit.
  //   DON'T CHANGE THE LOCATIONS OF THE INPUTS AND OUTPUTS!
  //   OUTPUTS from your circuit
endmodule
