// Logisim project cpu.circ as structural Verilog: 8 circuits, main circuit main
module main (
  input  [31:0] INSTRUCTION,
  input  CLOCK,
  output [31:0] FETCH_ADDRESS,
  output [31:0] ra_Value,
  output [31:0] sp_Value,
  output [31:0] t0_Value,
  output [31:0] t1_Value,
  output [31:0] t2_Value,
  output [31:0] s0_Value,
  output [31:0] s1_Value,
  output [31:0] a0_Value
);

  wire ASel, BrEq, BrLt, BrUn, BSel, MemRW, PCSel, RegWEn, SwgeSel;
  wire [1:0] select_bit, WBSel;
  wire [2:0] funct3, ImmSel;
  wire [3:0] ALUSel;
  wire [6:0] funct7;
  wire [24:0] Inst_Delay;
  wire [31:0] alu, divider_1_out, imm, mem, MEM_p7, multiplexer_1_out, multiplexer_2_out, multiplexer_3_out,
       multiplexer_4_out, multiplexer_5_out, multiplexer_6_out, multiplexer_8_out, PC, PC_4, PC_q,
       plus4_out_2, R_rs1, R_rs2, write_data;
  wire [31:2] divider_1_rem;

  Multiplexer #(.width(32), .enable("false")) multiplexer_1 (
    .in0(PC_4), .in1(alu), .out(multiplexer_1_out), .sel(PCSel));
  Register #(.width(32)) u_PC (.D(multiplexer_1_out), .en(CLOCK), .Q(PC_q), .clk(CLOCK));  // open: clr
  // Probe on INSTRUCTION
  // Probe on {funct7, Inst_Delay[24:15], funct3, Inst_Delay[11:0]}
  // Probe on PC
  // Probe on R_rs1
  // Probe on R_rs2
  // Probe on imm
  // Probe on alu
  // Probe on write_data
  // Probe on mem
  // Probe on mem
  plus4 plsu4 (.in_1(PC_q), .out_2(PC_4));
  align_address align_address (.in_1(PC_q), .out_2(FETCH_ADDRESS));
  Register #(.width(32)) PCd (.D(PC_q), .en(CLOCK), .Q(PC), .clk(CLOCK));  // open: clr
  // Probe on select_bit
  // Probe on BrEq
  // Probe on BrLt
  regfile_main main_1 (
    .Read_Register_1__rs1(Inst_Delay[19:15]), .Read_Register_2__rs2(Inst_Delay[24:20]),
    .Write_Register__rd(Inst_Delay[11:7]), .Write_Data(write_data), .Write_Enable(RegWEn), .Clock(CLOCK),
    .Read_Data_1(R_rs1), .Read_Data_2(R_rs2), .ra_Value(ra_Value), .sp_Value(sp_Value), .t0_Value(t0_Value),
    .t1_Value(t1_Value), .t2_Value(t2_Value), .s0_Value(s0_Value), .s1_Value(s1_Value), .a0_Value(a0_Value));
  // Probe on PCSel
  // Probe on ImmSel
  // Probe on BrUn
  // Probe on RegWEn
  // Probe on ASel
  // Probe on BSel
  // Probe on ALUSel
  // Probe on MemRW
  // Probe on WBSel
  // Probe on SwgeSel
  Multiplexer #(.width(32), .enable("false")) multiplexer_2 (
    .in0(R_rs1), .in1(PC), .out(multiplexer_2_out), .sel(ASel));
  Multiplexer #(.width(32), .enable("false")) multiplexer_3 (
    .in0(multiplexer_2_out), .in1({32{1'b0}}), .out(multiplexer_3_out), .sel(SwgeSel));
  Multiplexer #(.width(32), .enable("false")) multiplexer_4 (
    .in0(R_rs2), .in1(imm), .out(multiplexer_4_out), .sel(BSel));
  alu_main main_2 (.Switch(ALUSel), .X(multiplexer_3_out), .Result(alu), .Y(multiplexer_4_out));  // open: Equal
  // Probe on multiplexer_4_out
  // Probe on multiplexer_4_out
  Multiplexer #(.width(32), .enable("false")) multiplexer_5 (
    .in0(INSTRUCTION), .in1({32{1'b0}}), .out(multiplexer_5_out), .sel(PCSel));
  // Probe on {funct7, Inst_Delay[24:15], funct3, Inst_Delay[11:0]}
  // Probe on multiplexer_3_out
  Register #(.width(32)) Instd (
    .D(multiplexer_5_out), .en(CLOCK), .Q({funct7, Inst_Delay[24:15], funct3, Inst_Delay[11:0]}), .clk(CLOCK));  // open: clr
  Imm_Gen imm_gen_1 (.in_1({funct7, Inst_Delay[24:15], funct3, Inst_Delay[11:0]}), .ImmSel(ImmSel), .out_3(imm));
  Multiplexer #(.width(32), .enable("false")) multiplexer_6 (
    .in0(alu), .in1(R_rs1), .out(multiplexer_6_out), .sel(SwgeSel));
  // Probe on multiplexer_6_out
  Divider #(.width(32)) divider_1 (
    .a(multiplexer_6_out), .b(32'h4), .out(divider_1_out), .rem({divider_1_rem, select_bit}));  // open: upper
  // mem_main MEM: pin names not known; wires that end beside it: {divider_1_rem, select_bit}, divider_1_out, divider_1_out, R_rs2, MemRW, CLOCK, MEM_p7
  Control_Logic control_logic_1 (
    ._32_Bit_Instruction({funct7, Inst_Delay[24:15], funct3, Inst_Delay[11:0]}), .BrEq(BrEq), .BrLt(BrLt),
    .PCSel(PCSel), .ImmSel(ImmSel), .BrUn(BrUn), .RegWEn(RegWEn), .ASel(ASel), .BSel(BSel), .ALUSel(ALUSel),
    .MemRW(MemRW), .WBSel(WBSel), .SwagSel(SwgeSel));
  // Probe on mem
  Load_Selector load_selector_1 (.in_1(MEM_p7), .funct3(funct3), .bitSelector(select_bit), .mem(mem));
  plus4 plus4 (.in_1(PC), .out_2(plus4_out_2));
  // Probe on write_data
  Multiplexer #(.select(2), .width(32), .enable("false")) multiplexer_7 (
    .in0(mem), .in1(alu), .in2(plus4_out_2), .out(write_data), .sel(WBSel));  // open: in3
  Multiplexer #(.width(32), .enable("false")) multiplexer_8 (
    .in0(R_rs1), .in1(imm), .out(multiplexer_8_out), .sel(SwgeSel));
  Branch_Comp branch_comp_1 (.in_1(multiplexer_8_out), .in_2(R_rs2), .BrUn(BrUn), .BrEq(BrEq), .BrLt(BrLt));

  // Other names for the same wires on the sheet: a0[31:0] = a0_Value; clk = CLOCK; fetch_addr[31:0] = FETCH_ADDRESS;
  //   opcode[6:0] = Inst_Delay[6:0]; rd[4:0] = Inst_Delay[11:7]; Inst_Delay (some bits) = {funct7, funct3};
  //   rs1[4:0] = Inst_Delay[19:15]; rs2[4:0] = Inst_Delay[24:20]; ra[31:0] = ra_Value; s0[31:0] = s0_Value;
  //   s1[31:0] = s1_Value; sp[31:0] = sp_Value; t0[31:0] = t0_Value; t1[31:0] = t1_Value; t2[31:0] = t2_Value

  // Notes on the sheet:
  //   Debug Only:
  //   Output
  //   These are outputs/inputs from run.circ
  //   Inputs
  //   No Operation
endmodule

module plus4 (
  input  [31:0] in_1,
  output [31:0] out_2
);

  Adder #(.width(32)) adder_1 (.a(32'h4), .b(in_1), .out(out_2));  // open: cin, cout
endmodule

module align_address (
  input  [31:0] in_1,
  output [31:0] out_2
);

  Shifter #(.width(32), .shift("lr")) shifter_1 (.in(in_1), .\dist (5'b00010), .out(out_2));
endmodule

module Control_Logic (
  input  [31:0] _32_Bit_Instruction,
  input  BrEq,
  input  BrLt,
  output PCSel,
  output [2:0] ImmSel,
  output BrUn,
  output RegWEn,
  output ASel,
  output BSel,
  output [3:0] ALUSel,
  output MemRW,
  output [1:0] WBSel,
  output SwagSel
);

  wire and_1_out, and_2_out, and_3_out, and_7_out, and_10_out, and_11_out, and_12_out, and_13_out,
       and_14_out, and_15_out, and_16_out, and_17_out, and_18_out, and_19_out, and_20_out, and_21_out,
       and_22_out, and_23_out, and_24_out, and_25_out, and_26_out, and_27_out, and_28_out, and_29_out,
       comparator_1_eq, comparator_2_eq, comparator_3_eq, comparator_4_eq, comparator_6_eq, comparator_15_eq,
       comparator_16_eq, comparator_19_eq, comparator_20_eq, comparator_21_eq, comparator_22_eq,
       comparator_23_eq, comparator_24_eq, comparator_25_eq, comparator_26_eq, comparator_27_eq,
       comparator_28_eq, comparator_29_eq, comparator_30_eq, comparator_31_eq, comparator_32_eq,
       comparator_33_eq, comparator_34_eq, comparator_35_eq, comparator_36_eq, comparator_37_eq,
       comparator_38_eq, comparator_39_eq, comparator_40_eq, comparator_41_eq, comparator_42_eq,
       comparator_43_eq, comparator_44_eq, comparator_45_eq, comparator_46_eq, comparator_47_eq,
       comparator_48_eq, comparator_49_eq, comparator_50_eq, comparator_51_eq, i_type, i_type_jalr,
       i_type_load, isNOP, not_1_out, not_2_out, not_3_out, not_4_out, or_1_out, or_2_out, or_6_out,
       or_7_out, or_8_out, or_9_out, or_10_out, or_11_out, or_12_out, or_13_out, or_14_out, or_15_out,
       or_16_out, or_17_out, r_type, s_type, sb_type, u_type_lui, uj_type;
  wire [0:0] comparator_18_eq;
  wire [1:1] comparator_17_eq;
  wire [2:0] adder_1_out, adder_2_out;
  wire [3:0] ALU_Add, ALU_And, ALU_Div, ALU_Mul, ALU_Mulh, ALU_Or, ALU_Rem, ALU_Sll, ALU_Slt, ALU_Sra,
       ALU_Srl, ALU_Xor;

  Comparator #(.width(3)) comparator_1 (
    .a(3'b000), .b(_32_Bit_Instruction[14:12]), .eq(comparator_1_eq));  // open: gt, lt
  Comparator #(.width(1)) comparator_2 (.a(1'b1), .b(_32_Bit_Instruction[14]), .eq(comparator_2_eq));  // open: gt, lt
  Comparator #(.width(7)) comparator_3 (
    .a(7'b1100011), .b(_32_Bit_Instruction[6:0]), .eq(comparator_3_eq));  // open: gt, lt
  Comparator #(.width(3)) comparator_4 (
    .a(3'b110), .b(_32_Bit_Instruction[14:12]), .eq(comparator_4_eq));  // open: gt, lt
  Comparator #(.width(32)) comparator_5 (.a(_32_Bit_Instruction), .b({32{1'b0}}), .eq(isNOP));  // open: gt, lt
  and and_1 (and_1_out, BrEq, comparator_1_eq);
  and and_2 (and_2_out, BrLt, comparator_2_eq);
  or or_1 (or_1_out, and_1_out, and_2_out);
  Comparator #(.width(3)) comparator_6 (
    .a(_32_Bit_Instruction[14:12]), .b(3'b111), .eq(comparator_6_eq));  // open: gt, lt
  Comparator #(.width(7)) comparator_7 (.a(_32_Bit_Instruction[6:0]), .b(7'b0110011), .eq(r_type));  // open: gt, lt
  Comparator #(.width(7)) comparator_8 (
    .a(_32_Bit_Instruction[6:0]), .b(7'b0000011), .eq(i_type_load));  // open: gt, lt
  Comparator #(.width(7)) comparator_9 (.a(_32_Bit_Instruction[6:0]), .b(7'b0010011), .eq(i_type));  // open: gt, lt
  Comparator #(.width(7)) comparator_10 (
    .a(_32_Bit_Instruction[6:0]), .b(7'b1100111), .eq(i_type_jalr));  // open: gt, lt
  Comparator #(.width(7)) comparator_11 (.a(_32_Bit_Instruction[6:0]), .b(7'b0100011), .eq(s_type));  // open: gt, lt
  Comparator #(.width(7)) comparator_12 (.a(_32_Bit_Instruction[6:0]), .b(7'b1100011), .eq(sb_type));  // open: gt, lt
  Comparator #(.width(7)) comparator_13 (
    .a(_32_Bit_Instruction[6:0]), .b(7'b0110111), .eq(u_type_lui));  // open: gt, lt
  Comparator #(.width(7)) comparator_14 (.a(_32_Bit_Instruction[6:0]), .b(7'b1101111), .eq(uj_type));  // open: gt, lt
  and and_3 (and_3_out, or_1_out, sb_type);
  or or_2 (or_2_out, uj_type, i_type_jalr);
  and and_4 (BrUn, comparator_3_eq, comparator_4_eq);
  or or_3 (ASel, uj_type, sb_type);
  or or_4 (PCSel, and_3_out, or_2_out);
  assign ALUSel = ALU_Add | ALU_And | ALU_Or | ALU_Xor | ALU_Srl | ALU_Sra | ALU_Sll | ALU_Slt | ALU_Div | ALU_Rem | ALU_Mul | ALU_Mulh;  // OR_Gate or_5, 4 bits wide
  and and_5 (SwagSel, s_type, comparator_6_eq);
  not not_1 (not_1_out, SwagSel);
  not not_2 (not_2_out, r_type);
  Comparator #(.width(3)) comparator_15 (
    .a(_32_Bit_Instruction[14:12]), .b(3'b111), .eq(comparator_15_eq));  // open: gt, lt
  Comparator #(.width(3)) comparator_16 (
    .a(_32_Bit_Instruction[14:12]), .b(3'b010), .eq(comparator_16_eq));  // open: gt, lt
  Adder #(.width(3)) adder_1 (.a({2'b00, s_type}), .b({1'b0, sb_type, 1'b0}), .out(adder_1_out));  // open: cin, cout
  Adder #(.width(3)) adder_2 (.a({1'b0, {2{u_type_lui}}}), .b({uj_type, 2'b00}), .out(adder_2_out));  // open: cin, cout
  or or_6 (or_6_out, s_type, sb_type);
  and and_6 (BSel, not_1_out, not_2_out);
  and and_7 (and_7_out, BrLt, comparator_15_eq);
  or or_7 (or_7_out, uj_type, i_type_jalr);
  or or_8 (or_8_out, r_type, sb_type, i_type, u_type_lui);
  not not_3 (not_3_out, isNOP);
  not not_4 (not_4_out, or_6_out);
  or or_9 (or_9_out, and_7_out, comparator_16_eq);
  Comparator #(.width(1)) comparator_17 (.a(1'b1), .b(or_7_out), .eq(comparator_17_eq[1]));  // open: gt, lt
  Comparator #(.width(1)) comparator_18 (.a(1'b1), .b(or_8_out), .eq(comparator_18_eq[0]));  // open: gt, lt
  Adder #(.width(3)) adder_3 (.a(adder_1_out), .b(adder_2_out), .out(ImmSel));  // open: cin, cout
  and and_8 (RegWEn, not_3_out, not_4_out);
  and and_9 (MemRW, or_9_out, s_type);
  Adder #(.width(2)) adder_4 (
    .a({comparator_17_eq[1], 1'b0}), .b({1'b0, comparator_18_eq[0]}), .out(WBSel));  // open: cin, cout
  Comparator #(.width(3)) comparator_19 (
    .a(_32_Bit_Instruction[14:12]), .b(3'b000), .eq(comparator_19_eq));  // open: gt, lt
  Comparator #(.width(7)) comparator_20 (
    .a(_32_Bit_Instruction[31:25]), .b({7{1'b0}}), .eq(comparator_20_eq));  // open: gt, lt
  Comparator #(.width(3)) comparator_21 (
    .a(_32_Bit_Instruction[14:12]), .b(3'b000), .eq(comparator_21_eq));  // open: gt, lt
  Comparator #(.width(3)) comparator_22 (
    .a(_32_Bit_Instruction[14:12]), .b(3'b110), .eq(comparator_22_eq));  // open: gt, lt
  Comparator #(.width(7)) comparator_23 (
    .a(_32_Bit_Instruction[31:25]), .b({7{1'b0}}), .eq(comparator_23_eq));  // open: gt, lt
  Comparator #(.width(3)) comparator_24 (
    .a(_32_Bit_Instruction[14:12]), .b(3'b110), .eq(comparator_24_eq));  // open: gt, lt
  Comparator #(.width(3)) comparator_25 (
    .a(_32_Bit_Instruction[14:12]), .b(3'b101), .eq(comparator_25_eq));  // open: gt, lt
  Comparator #(.width(7)) comparator_26 (
    .a(_32_Bit_Instruction[31:25]), .b(7'b0100000), .eq(comparator_26_eq));  // open: gt, lt
  Comparator #(.width(3)) comparator_27 (
    .a(_32_Bit_Instruction[14:12]), .b(3'b101), .eq(comparator_27_eq));  // open: gt, lt
  Comparator #(.width(3)) comparator_28 (
    .a(_32_Bit_Instruction[14:12]), .b(3'b010), .eq(comparator_28_eq));  // open: gt, lt
  Comparator #(.width(7)) comparator_29 (
    .a(_32_Bit_Instruction[31:25]), .b({7{1'b0}}), .eq(comparator_29_eq));  // open: gt, lt
  Comparator #(.width(3)) comparator_30 (
    .a(_32_Bit_Instruction[14:12]), .b(3'b010), .eq(comparator_30_eq));  // open: gt, lt
  Comparator #(.width(3)) comparator_31 (
    .a(_32_Bit_Instruction[14:12]), .b(3'b100), .eq(comparator_31_eq));  // open: gt, lt
  Comparator #(.width(7)) comparator_32 (
    .a(_32_Bit_Instruction[31:25]), .b(7'b0000001), .eq(comparator_32_eq));  // open: gt, lt
  Comparator #(.width(3)) comparator_33 (
    .a(_32_Bit_Instruction[14:12]), .b(3'b110), .eq(comparator_33_eq));  // open: gt, lt
  Comparator #(.width(7)) comparator_34 (
    .a(_32_Bit_Instruction[31:25]), .b(7'b0000001), .eq(comparator_34_eq));  // open: gt, lt
  and and_10 (and_10_out, r_type, comparator_19_eq, comparator_20_eq);
  and and_11 (and_11_out, i_type, comparator_21_eq);
  and and_12 (and_12_out, r_type, comparator_25_eq, comparator_26_eq);
  and and_13 (and_13_out, i_type, comparator_27_eq);
  and and_14 (and_14_out, r_type, comparator_28_eq, comparator_29_eq);
  and and_15 (and_15_out, i_type, comparator_30_eq);
  and and_16 (and_16_out, r_type, comparator_31_eq, comparator_32_eq);
  and and_17 (and_17_out, r_type, comparator_33_eq, comparator_34_eq);
  and and_18 (and_18_out, r_type, comparator_22_eq, comparator_23_eq);
  or or_10 (or_10_out, and_18_out, and_19_out);
  and and_19 (and_19_out, i_type, comparator_24_eq);
  or or_11 (or_11_out, and_12_out, and_13_out);
  or or_12 (or_12_out, and_14_out, and_15_out);
  Demultiplexer #(.width(4), .enable("false")) demultiplexer_1 (
    .out1(ALU_Add), .in(4'b0000), .sel(or_13_out));  // open: out0
  or or_13 (or_13_out, and_10_out, and_11_out, i_type_load, s_type, sb_type, u_type_lui, uj_type);
  Demultiplexer #(.width(4), .enable("false")) demultiplexer_2 (
    .out1(ALU_Or), .in(4'b0010), .sel(or_10_out));  // open: out0
  Demultiplexer #(.width(4), .enable("false")) demultiplexer_3 (
    .out1(ALU_Sra), .in(4'b0101), .sel(or_11_out));  // open: out0
  Demultiplexer #(.width(4), .enable("false")) demultiplexer_4 (
    .out1(ALU_Slt), .in(4'b0111), .sel(or_12_out));  // open: out0
  Demultiplexer #(.width(4), .enable("false")) demultiplexer_5 (
    .out1(ALU_Div), .in(4'b1000), .sel(and_16_out));  // open: out0
  Demultiplexer #(.width(4), .enable("false")) demultiplexer_6 (
    .out1(ALU_Rem), .in(4'b1001), .sel(and_17_out));  // open: out0
  Comparator #(.width(3)) comparator_35 (
    .a(_32_Bit_Instruction[14:12]), .b(3'b111), .eq(comparator_35_eq));  // open: gt, lt
  Comparator #(.width(7)) comparator_36 (
    .a(_32_Bit_Instruction[31:25]), .b({7{1'b0}}), .eq(comparator_36_eq));  // open: gt, lt
  Comparator #(.width(3)) comparator_37 (
    .a(_32_Bit_Instruction[14:12]), .b(3'b111), .eq(comparator_37_eq));  // open: gt, lt
  Comparator #(.width(3)) comparator_38 (
    .a(_32_Bit_Instruction[14:12]), .b(3'b100), .eq(comparator_38_eq));  // open: gt, lt
  Comparator #(.width(7)) comparator_39 (
    .a(_32_Bit_Instruction[31:25]), .b({7{1'b0}}), .eq(comparator_39_eq));  // open: gt, lt
  Comparator #(.width(3)) comparator_40 (
    .a(_32_Bit_Instruction[14:12]), .b(3'b100), .eq(comparator_40_eq));  // open: gt, lt
  Comparator #(.width(3)) comparator_41 (
    .a(_32_Bit_Instruction[14:12]), .b(3'b101), .eq(comparator_41_eq));  // open: gt, lt
  Comparator #(.width(7)) comparator_42 (
    .a(_32_Bit_Instruction[31:25]), .b({7{1'b0}}), .eq(comparator_42_eq));  // open: gt, lt
  Comparator #(.width(3)) comparator_43 (
    .a(_32_Bit_Instruction[14:12]), .b(3'b101), .eq(comparator_43_eq));  // open: gt, lt
  Comparator #(.width(3)) comparator_44 (
    .a(_32_Bit_Instruction[14:12]), .b(3'b001), .eq(comparator_44_eq));  // open: gt, lt
  Comparator #(.width(7)) comparator_45 (
    .a(_32_Bit_Instruction[31:25]), .b({7{1'b0}}), .eq(comparator_45_eq));  // open: gt, lt
  Comparator #(.width(3)) comparator_46 (
    .a(_32_Bit_Instruction[14:12]), .b(3'b001), .eq(comparator_46_eq));  // open: gt, lt
  Comparator #(.width(7)) comparator_47 (
    .a(_32_Bit_Instruction[31:25]), .b({7{1'b0}}), .eq(comparator_47_eq));  // open: gt, lt
  Comparator #(.width(3)) comparator_48 (
    .a(_32_Bit_Instruction[14:12]), .b(3'b000), .eq(comparator_48_eq));  // open: gt, lt
  Comparator #(.width(7)) comparator_49 (
    .a(_32_Bit_Instruction[31:25]), .b(7'b0000001), .eq(comparator_49_eq));  // open: gt, lt
  Comparator #(.width(3)) comparator_50 (
    .a(_32_Bit_Instruction[14:12]), .b(3'b001), .eq(comparator_50_eq));  // open: gt, lt
  Comparator #(.width(7)) comparator_51 (
    .a(_32_Bit_Instruction[31:25]), .b(7'b0000001), .eq(comparator_51_eq));  // open: gt, lt
  and and_20 (and_20_out, r_type, comparator_35_eq, comparator_36_eq);
  and and_21 (and_21_out, i_type, comparator_37_eq);
  and and_22 (and_22_out, r_type, comparator_38_eq, comparator_39_eq);
  and and_23 (and_23_out, i_type, comparator_40_eq);
  and and_24 (and_24_out, r_type, comparator_41_eq, comparator_42_eq);
  and and_25 (and_25_out, i_type, comparator_43_eq);
  and and_26 (and_26_out, r_type, comparator_44_eq, comparator_45_eq);
  and and_27 (and_27_out, i_type, comparator_46_eq, comparator_47_eq);
  and and_28 (and_28_out, r_type, comparator_48_eq, comparator_49_eq);
  and and_29 (and_29_out, r_type, comparator_50_eq, comparator_51_eq);
  or or_14 (or_14_out, and_20_out, and_21_out);
  or or_15 (or_15_out, and_22_out, and_23_out);
  or or_16 (or_16_out, and_24_out, and_25_out);
  or or_17 (or_17_out, and_26_out, and_27_out);
  Demultiplexer #(.width(4), .enable("false")) demultiplexer_7 (
    .out1(ALU_And), .in(4'b0001), .sel(or_14_out));  // open: out0
  Demultiplexer #(.width(4), .enable("false")) demultiplexer_8 (
    .out1(ALU_Xor), .in(4'b0011), .sel(or_15_out));  // open: out0
  Demultiplexer #(.width(4), .enable("false")) demultiplexer_9 (
    .out1(ALU_Srl), .in(4'b0100), .sel(or_16_out));  // open: out0
  Demultiplexer #(.width(4), .enable("false")) demultiplexer_10 (
    .out1(ALU_Sll), .in(4'b0110), .sel(or_17_out));  // open: out0
  Demultiplexer #(.width(4), .enable("false")) demultiplexer_11 (
    .out1(ALU_Mul), .in(4'b1010), .sel(and_28_out));  // open: out0
  Demultiplexer #(.width(4), .enable("false")) demultiplexer_12 (
    .out1(ALU_Mulh), .in(4'b1011), .sel(and_29_out));  // open: out0

  // Other names for the same wires on the sheet: op[6:0] = _32_Bit_Instruction[6:0];
  //   funct3[2:0] = _32_Bit_Instruction[14:12]; funct7[6:0] = _32_Bit_Instruction[31:25]; SwgeSel = SwagSel

  // Notes on the sheet:
  //   PCSel:
  //   BrUn:
  //   ALUSel:
  //   Instruction Type
  //   ImmSel:
  //   RegWEn:
  //   BSel:
  //   MemRW:
  //   WBSel:
endmodule

module Imm_Gen (
  input  [31:0] in_1,
  input  [2:0] ImmSel,
  output [31:0] out_3
);

  wire [11:0] shifter_1_out;
  wire [19:0] shifter_2_out;
  wire [31:0] bit_extender_1_out, bit_extender_2_out, bit_extender_3_out, bit_extender_4_out,
       bit_extender_5_out, shifter_3_out;

  Shifter #(.width(12)) shifter_1 (
    .in({in_1[31], in_1[7], in_1[30:25], in_1[11:8]}), .\dist (4'b0001), .out(shifter_1_out));
  Shifter #(.width(20)) shifter_2 (
    .in({in_1[31], in_1[19:12], in_1[20], in_1[30:21]}), .\dist (5'b00001), .out(shifter_2_out));
  assign bit_extender_1_out = {{20{in_1[31]}}, in_1[31:20]};  // Bit_Extender bit_extender_1
  assign bit_extender_2_out = {{20{in_1[31]}}, {in_1[31:25], in_1[11:7]}};  // Bit_Extender bit_extender_2
  assign bit_extender_3_out = {{20{shifter_1_out[11]}}, shifter_1_out};  // Bit_Extender bit_extender_3
  assign bit_extender_4_out = {{12{in_1[31]}}, in_1[31:12]};  // Bit_Extender bit_extender_4
  assign bit_extender_5_out = {{12{shifter_2_out[19]}}, shifter_2_out};  // Bit_Extender bit_extender_5
  Shifter #(.width(32)) shifter_3 (.in(bit_extender_4_out), .\dist (5'b01100), .out(shifter_3_out));
  Multiplexer #(.select(3), .width(32), .disabled(0), .enable("false")) multiplexer_1 (
    .in0(bit_extender_1_out), .in1(bit_extender_2_out), .in2(bit_extender_3_out), .in3(shifter_3_out),
    .in4(bit_extender_5_out), .out(out_3), .sel(ImmSel));  // open: in5, in6, in7

  // Notes on the sheet:
  //   I-Type
  //   S-Type
  //   B-Type
  //   U-Type
  //   J-Type
endmodule

module Branch_Comp (
  input  [31:0] in_1,
  input  [31:0] in_2,
  input  BrUn,
  output BrEq,
  output BrLt
);

  wire comparator_1_eq, comparator_1_lt, comparator_2_eq, comparator_2_lt;

  Comparator #(.width(32)) comparator_1 (.a(in_1), .b(in_2), .eq(comparator_1_eq), .lt(comparator_1_lt));  // open: gt
  Comparator #(.width(32), .mode("unsigned")) comparator_2 (
    .a(in_1), .b(in_2), .eq(comparator_2_eq), .lt(comparator_2_lt));  // open: gt
  Multiplexer #(.enable("false")) multiplexer_1 (.in0(comparator_1_eq), .in1(comparator_2_eq), .out(BrEq), .sel(BrUn));
  Multiplexer #(.enable("false")) multiplexer_2 (.in0(comparator_1_lt), .in1(comparator_2_lt), .out(BrLt), .sel(BrUn));

  // Notes on the sheet:
  //   RS1 Value
  //   RS2 Value
  //   Signed
  //   Unsigned
endmodule

module Load_Selector (
  input  [31:0] in_1,
  input  [2:0] funct3,
  input  [1:0] bitSelector,
  output [31:0] mem
);

  wire [7:0] multiplexer_1_out;
  wire [15:0] multiplexer_2_out;
  wire [31:0] bit_extender_1_out, bit_extender_2_out;

  Multiplexer #(.select(2), .width(8), .enable("false")) multiplexer_1 (
    .in0(in_1[7:0]), .in1(in_1[15:8]), .in2(in_1[23:16]), .in3(in_1[31:24]), .out(multiplexer_1_out),
    .sel(bitSelector));
  Multiplexer #(.width(16), .enable("false")) multiplexer_2 (
    .in0(in_1[15:0]), .in1(in_1[31:16]), .out(multiplexer_2_out), .sel(bitSelector[0]));
  assign bit_extender_1_out = {{16{multiplexer_2_out[15]}}, multiplexer_2_out};  // Bit_Extender bit_extender_1
  assign bit_extender_2_out = {{24{multiplexer_1_out[7]}}, multiplexer_1_out};  // Bit_Extender bit_extender_2
  Multiplexer #(.select(3), .width(32), .disabled(0), .enable("false")) multiplexer_3 (
    .in0(bit_extender_2_out), .in1(bit_extender_1_out), .in2(in_1), .out(mem), .sel(funct3));  // open: in3, in4, in5, in6, in7

  // Other names for the same wires on the sheet: data_from_mem[31:0] = in_1; SelectByte[1:0] = bitSelector;
  //   SelectHalf = bitSelector[0]

  // Notes on the sheet:
  //   lb
  //   lh
  //   lw
endmodule

module temp (
  output [31:0] out_1,
  output [31:0] out_2
);

  wire i_type, i_type_jalr, r_type, s_type, sb_type, u_type_lui, uj_type;
  wire [0:0] or_2_out;
  wire [1:0] and_1_out, WBSel;
  wire [1:1] or_1_out;

  assign and_1_out = 2'b01 & 2'b10;  // AND_Gate and_1, 2 bits wide
  // Probe on and_1_out
  // Probe on 32'hffffff40
  or or_1 (or_1_out[1], uj_type, sb_type, i_type_jalr);
  or or_2 (or_2_out[0], r_type, s_type, u_type_lui, i_type);
  // Probe on 32'hfffff000
  // Probe on 32'hfffff000
  Adder #(.width(2)) adder_1 (.a({or_1_out[1], 1'b0}), .b({1'b0, or_2_out[0]}), .out(WBSel));  // open: cin, cout
  Subtractor #(.width(32)) subtractor_1 (.a({32{1'b0}}), .b({32{1'b0}}), .out(out_2));  // open: bin, bout

  assign out_1 = 32'hffffff40;

  // Notes on the sheet:
  //   ALU
endmodule
